// Logisim project oi.circ as structural Verilog: 3 circuits, main circuit main
module main (
  input  A,
  input  B,
  input  Vem1,
  output S,
  output Vai1
);

  wire and_1_out, and_2_out, and_3_out, xor_1_out;

  xor xor_1 (xor_1_out, A, B);
  and and_1 (and_1_out, A, Vem1);
  and and_2 (and_2_out, A, B);
  and and_3 (and_3_out, B, Vem1);
  xor xor_2 (S, xor_1_out, Vem1);
  or or_1 (Vai1, and_1_out, and_2_out, and_3_out);
endmodule

module Macro (
);

  main main_1 ();  // open: A, B, Vem1, S, Vai1
endmodule

module soma4bits (
  input  [3:0] B,
  input  in_2,
  output [3:0] A,
  output [3:0] out_4,
  output out_5
);

  wire main_1_p1, main_1_p5, main_3_p1, undriven_2;
  wire [3:0] undriven;

  // main main_1: pin names not known; wires that end beside it: main_1_p1, undriven[3], B[3], out_4[3], main_1_p5
  main main_2 (.A(undriven[2]), .B(B[2]), .Vem1(main_3_p1), .S(main_1_p5), .Vai1(out_4[2]));
  // main main_3: pin names not known; wires that end beside it: main_3_p1, undriven[1], B[1], out_4[1], out_4[0]
  main main_4 (.A(undriven[0]), .B(B[0]), .Vem1(undriven_2), .S(out_4[0]), .Vai1(out_4[0]));
endmodule
